# Fritzing sketch basic_module (saved by Fritzing 0.9.4)
breadboards: 1

parts:
  Part1 = Arduino Nano (Rev3.0) (ICSP)
  M1 = Niren can bus module [package=THT]
  R1 = Resistor [tolerance=±5% resistance=330 package=THT]
  LED1 = RGB LED (com. cathode, rbg) [package="5 mm [THT]"]
  R2 = Resistor [tolerance=±5% resistance=330 package="0603 [SMD]"]

nets:
  N1: Part1.GND, M1.pin2, LED1.common_cathode
  N2: Part1.D2, M1.pin7
  N3: Part1.D8, M1.pin3
  N4: Part1.D11/MOSI, M1.pin5
  N5: Part1.D12/MISO, M1.pin4
  N6: Part1.5V, M1.pin1
  N7: Part1.A5, R2.Pin_0
  N8: Part1.A4, R1.Pin_0
  N9: Part1.D13/SCK, M1.pin6
  N10: R1.Pin_1, LED1.red_anode
  N11: LED1.blue_anode, R2.Pin_1

custom parts:
  Niren can bus module: Niren can bus module availabe on ebay and others. Pcb view assumes that you unsolder the 7 pin header and resolder it on the bottom of the module to connect to the pcb. The two jumpers and the can bus connector remain on the top of the board and don't appear in pcb view.
